// Logisim project tp_exam.circ as structural Verilog: 1 circuit, main circuit main
module main (
  input  e0,
  input  e1,
  input  e2,
  input  e3,
  output s0,
  output s1,
  output s2,
  output s3
);

  wire and_1_out, and_2_out, and_3_out, not_1_out, not_2_out, not_3_out, not_4_out, or_1_out, or_2_out;

  not not_1 (not_1_out, e0);
  not not_2 (not_2_out, e1);
  not not_3 (not_3_out, e2);
  not not_4 (not_4_out, e2);
  and and_1 (and_1_out, not_1_out, not_2_out, e2);
  and and_2 (and_2_out, e0, not_3_out);
  and and_3 (and_3_out, e1, not_4_out);
  or or_1 (or_1_out, e2, e3);
  or or_2 (or_2_out, e0, e1);
  not not_5 (s0, e0);
  xnor xnor_1 (s1, e0, e1);
  or or_3 (s2, and_1_out, and_2_out, and_3_out);
  and and_4 (s3, or_1_out, or_2_out);
endmodule
