// Logisim project tp_exam_3.circ as structural Verilog: 4 circuits, main circuit question1
module question1 (
  input  e0,
  input  e1,
  input  e2,
  input  e3,
  output s0,
  output s1,
  output s2,
  output s3
);

  wire and_1_out, and_2_out, and_3_out, not_1_out, not_2_out, not_3_out, not_4_out, or_1_out, or_2_out;

  not not_1 (not_1_out, e0);
  not not_2 (not_2_out, e1);
  not not_3 (not_3_out, e2);
  not not_4 (not_4_out, e2);
  and and_1 (and_1_out, not_1_out, not_2_out, e2);
  and and_2 (and_2_out, e0, not_3_out);
  and and_3 (and_3_out, e1, not_4_out);
  or or_1 (or_1_out, e2, e3);
  or or_2 (or_2_out, e0, e1);
  not not_5 (s0, e0);
  xnor xnor_1 (s1, e0, e1);
  or or_3 (s2, and_1_out, and_2_out, and_3_out);
  and and_4 (s3, or_1_out, or_2_out);
endmodule

module sequenceur (
  input  in_1,
  output s0,
  output s2,
  output s1,
  output s3
);

  wire and_1_out, d_ff_1_q, d_ff_1_qn, d_ff_2_q, d_ff_2_qn, d_ff_3_q, d_ff_3_qn, d_ff_4_q, d_ff_4_qn;

  D_Flip_Flop d_ff_1 (.D(d_ff_1_qn), .clk(in_1), .Q(d_ff_1_q), .Qn(d_ff_1_qn), .preset(and_1_out));  // open: reset
  not not_1 (s0, d_ff_1_q);
  D_Flip_Flop d_ff_2 (.D(d_ff_2_qn), .clk(d_ff_1_q), .Q(d_ff_2_q), .Qn(d_ff_2_qn), .preset(and_1_out));  // open: reset
  not not_2 (s1, d_ff_2_q);
  D_Flip_Flop d_ff_3 (.D(d_ff_3_qn), .clk(d_ff_2_q), .Q(d_ff_3_q), .Qn(d_ff_3_qn), .preset(and_1_out));  // open: reset
  not not_3 (s2, d_ff_3_q);
  D_Flip_Flop d_ff_4 (.D(d_ff_4_qn), .clk(d_ff_3_q), .Q(d_ff_4_q), .Qn(d_ff_4_qn), .preset(and_1_out));  // open: reset
  not not_4 (s3, d_ff_4_q);
  and and_1 (and_1_out, s1, s2);
endmodule

module question2 (
);

  wire clock_1_out;
  wire [3:0] sequenceur_1_s0;

  Clock clock_1 (.out(clock_1_out));
  sequenceur sequenceur_1 (
    .in_1(clock_1_out), .s0(sequenceur_1_s0[0]), .s2(sequenceur_1_s0[2]), .s1(sequenceur_1_s0[1]),
    .s3(sequenceur_1_s0[3]));
  Hex_Digit_Display hex_digit_display_1 (.value(sequenceur_1_s0));  // open: dp
endmodule

module question3 (
);

  wire clock_1_out, sequenceur_1_s0, sequenceur_1_s1, sequenceur_1_s2, sequenceur_1_s3;
  wire [3:0] question1_1_s0;

  Clock clock_1 (.out(clock_1_out));
  sequenceur sequenceur_1 (
    .in_1(clock_1_out), .s0(sequenceur_1_s0), .s2(sequenceur_1_s2), .s1(sequenceur_1_s1), .s3(sequenceur_1_s3));
  question1 question1_1 (
    .e0(sequenceur_1_s0), .e1(sequenceur_1_s1), .e2(sequenceur_1_s2), .e3(sequenceur_1_s3),
    .s0(question1_1_s0[0]), .s1(question1_1_s0[1]), .s2(question1_1_s0[2]), .s3(question1_1_s0[3]));
  Hex_Digit_Display hex_digit_display_1 (.value(question1_1_s0));  // open: dp
endmodule
