// Logisim project Projet1.circ as structural Verilog: 2 circuits, main circuit nor_nand
module nor_nand (
  input  a,
  input  b,
  output s0,
  output s1
);

  nor nor_1 (s0, a, b);
  nand nand_1 (s1, a, b);
endmodule

module or_and (
  input  e1,
  input  e0,
  output s1,
  output s0
);

  wire N0_s0, N0_s1;

  nor_nand N0 (.a(e1), .b(e0), .s0(N0_s0), .s1(N0_s1));
  nor_nand N1 (.a(N0_s0), .b(N0_s1), .s0(s1), .s1(s0));
endmodule
