// Logisim project Projet3.circ as structural Verilog: 1 circuit, main circuit main
module main (
  input  [3:0] A,
  input  [3:0] B,
  output [3:0] S
);

  assign S = A & B;  // AND_Gate and_1, 4 bits wide
endmodule
