// Logisim project Projet5.circ as structural Verilog: 1 circuit, main circuit main
module main (
  input  a,
  input  b,
  output s0,
  output s1,
  output s2
);

  wire not_1_out;

  not not_1 (not_1_out, a);
  or or_1 (s0, not_1_out, b);
  and and_1 (s1, a, b);
  or or_2 (s2, b, a);
endmodule
