// Logisim project Projet6.circ as structural Verilog: 1 circuit, main circuit main
module main (
  input  a,
  input  b,
  input  c,
  input  d,
  output s1,
  output s0
);

  wire and_1_out, and_2_out, and_3_out, and_4_out, and_5_out, not_1_out, not_2_out, not_3_out, not_4_out,
       or_1_out, or_2_out, or_3_out, or_4_out, or_5_out, or_6_out;

  not not_1 (not_1_out, a);
  not not_2 (not_2_out, b);
  not not_3 (not_3_out, c);
  not not_4 (not_4_out, d);
  or or_1 (or_1_out, a, c, d);
  or or_2 (or_2_out, b, c, d);
  or or_3 (or_3_out, not_2_out, not_3_out, not_4_out);
  or or_4 (or_4_out, not_1_out, not_3_out, not_4_out);
  or or_5 (or_5_out, not_1_out, not_2_out, not_4_out);
  or or_6 (or_6_out, not_1_out, not_2_out, not_3_out);
  and and_1 (and_1_out, not_1_out, not_2_out);
  and and_2 (and_2_out, not_1_out, not_3_out);
  and and_3 (and_3_out, not_2_out, not_3_out, d);
  and and_4 (and_4_out, not_2_out, c, not_4_out);
  and and_5 (and_5_out, a, b, c);
  and and_6 (s1, or_1_out, or_2_out, or_3_out, or_4_out, or_5_out, or_6_out);
  or or_7 (s0, and_1_out, and_2_out, and_3_out, and_4_out, and_5_out);
endmodule
