// Logisim project Projet7.circ as structural Verilog: 1 circuit, main circuit main
module main (
  input  e3,
  input  e2,
  input  e1,
  input  e0,
  output [1:0] s
);

  // Probe on {e2, e3}
  // Probe on {e0, e1, e2, e3}
  // Probe on {e0, e1}
  assign s = {e2, e3} & {e0, e1};  // AND_Gate and_1, 2 bits wide
endmodule
