// Logisim project tp2.circ as structural Verilog: 7 circuits, main circuit main
module main (
  input  [3:0] E,
  input  [3:0] in_2
);

  wire aff7dec_1_a, aff7dec_1_b, aff7dec_1_c, aff7dec_1_d, aff7dec_1_e, aff7dec_1_f, aff7dec_1_g,
       aff7hexa_1_a, aff7hexa_1_b, aff7hexa_1_c, aff7hexa_1_d, aff7hexa_1_e, aff7hexa_1_f, aff7hexa_1_g;

  aff7hexa aff7hexa_1 (
    .e0(E[0]), .e1(E[1]), .e2(E[2]), .e3(E[3]), .a(aff7hexa_1_a), .b(aff7hexa_1_b), .c(aff7hexa_1_c),
    .d(aff7hexa_1_d), .e(aff7hexa_1_e), .f(aff7hexa_1_f), .g(aff7hexa_1_g));
  aff7dec aff7dec_1 (
    .e0(in_2[0]), .e1(in_2[1]), .e2(in_2[2]), .e3(in_2[3]), .a(aff7dec_1_a), .b(aff7dec_1_b),
    .c(aff7dec_1_c), .d(aff7dec_1_d), .e(aff7dec_1_e), .f(aff7dec_1_f), .g(aff7dec_1_g));
  _7_Segment_Display u_7_segment_display_1 (
    .g(aff7hexa_1_g), .f(aff7hexa_1_f), .a(aff7hexa_1_a), .b(aff7hexa_1_b), .e(aff7hexa_1_e),
    .d(aff7hexa_1_d), .c(aff7hexa_1_c));  // open: dp
  _7_Segment_Display u_7_segment_display_2 (
    .g(aff7dec_1_g), .f(aff7dec_1_f), .a(aff7dec_1_a), .b(aff7dec_1_b), .e(aff7dec_1_e), .d(aff7dec_1_d),
    .c(aff7dec_1_c));  // open: dp
endmodule

module aff7hexa (
  input  e0,
  input  e1,
  input  e2,
  input  e3,
  output a,
  output b,
  output c,
  output d,
  output e,
  output f,
  output g
);

  wire and_1_out, and_2_out, and_3_out, and_4_out, and_5_out, and_6_out, and_7_out, and_8_out, and_9_out,
       and_10_out, and_11_out, and_12_out, and_13_out, and_14_out, and_15_out, and_16_out, and_17_out,
       and_18_out, and_19_out, and_20_out, and_21_out, and_22_out, and_23_out, and_24_out, and_25_out,
       and_26_out, and_27_out, and_28_out, and_29_out, and_30_out, and_31_out, and_32_out, and_33_out,
       and_34_out, and_35_out, and_36_out, not_1_out, not_2_out, not_3_out, not_4_out;

  not not_1 (not_1_out, e0);
  not not_2 (not_2_out, e1);
  not not_3 (not_3_out, e2);
  not not_4 (not_4_out, e3);
  and and_1 (and_1_out, not_2_out, not_4_out);
  and and_2 (and_2_out, not_1_out, e2);
  and and_3 (and_3_out, not_1_out, e1, e3);
  and and_4 (and_4_out, e1, e2);
  and and_5 (and_5_out, e0, not_2_out, not_3_out);
  and and_6 (and_6_out, e0, not_4_out);
  and and_7 (and_7_out, not_1_out, not_2_out);
  and and_8 (and_8_out, not_1_out, not_3_out, not_4_out);
  and and_9 (and_9_out, not_2_out, not_4_out);
  and and_10 (and_10_out, not_1_out, e2, e3);
  and and_11 (and_11_out, e0, not_3_out, e3);
  and and_12 (and_12_out, not_1_out, not_3_out);
  and and_13 (and_13_out, not_1_out, e3);
  and and_14 (and_14_out, not_3_out, e3);
  and and_15 (and_15_out, not_1_out, e1);
  and and_16 (and_16_out, e0, not_2_out);
  and and_17 (and_17_out, not_1_out, not_2_out, not_4_out);
  and and_18 (and_18_out, not_1_out, e2, not_4_out);
  and and_19 (and_19_out, not_2_out, e2, e3);
  and and_20 (and_20_out, e1, not_3_out, e3);
  and and_21 (and_21_out, e1, e2, not_4_out);
  and and_22 (and_22_out, e0, not_3_out);
  and and_23 (and_23_out, not_2_out, not_4_out);
  and and_24 (and_24_out, e2, not_4_out);
  and and_25 (and_25_out, e0, e2);
  and and_26 (and_26_out, e0, e1);
  and and_27 (and_27_out, not_3_out, not_4_out);
  and and_28 (and_28_out, not_1_out, e1, not_3_out);
  and and_29 (and_29_out, e1, not_4_out);
  and and_30 (and_30_out, e0, not_2_out);
  and and_31 (and_31_out, e0, e2);
  and and_32 (and_32_out, not_2_out, e2);
  and and_33 (and_33_out, e2, not_4_out);
  and and_34 (and_34_out, not_1_out, e1, not_3_out);
  and and_35 (and_35_out, e0, not_2_out);
  and and_36 (and_36_out, e0, e3);
  or or_1 (a, and_1_out, and_2_out, and_3_out, and_4_out, and_5_out, and_6_out);
  or or_2 (b, and_7_out, and_8_out, and_9_out, and_10_out, and_11_out);
  or or_3 (c, and_12_out, and_13_out, and_14_out, and_15_out, and_16_out);
  or or_4 (d, and_17_out, and_18_out, and_19_out, and_20_out, and_21_out, and_22_out);
  or or_5 (e, and_23_out, and_24_out, and_25_out, and_26_out);
  or or_6 (f, and_27_out, and_28_out, and_29_out, and_30_out, and_31_out);
  or or_7 (g, and_32_out, and_33_out, and_34_out, and_35_out, and_36_out);
endmodule

module aff7dec (
  input  e0,
  input  e1,
  input  e2,
  input  e3,
  output a,
  output b,
  output c,
  output d,
  output e,
  output f,
  output g
);

  wire and_1_out, and_2_out, and_3_out, and_4_out, and_5_out, and_6_out, and_7_out, and_8_out, and_9_out,
       and_10_out, and_11_out, and_12_out, and_13_out, and_14_out, and_15_out, and_16_out, and_17_out,
       and_18_out, and_19_out, and_20_out, and_21_out, and_22_out, and_23_out, and_24_out, and_25_out,
       and_26_out, not_1_out, not_2_out, not_3_out, not_4_out;

  not not_1 (not_1_out, e0);
  not not_2 (not_2_out, e1);
  not not_3 (not_3_out, e2);
  not not_4 (not_4_out, e3);
  and and_1 (and_1_out, not_1_out, not_2_out, not_4_out);
  and and_2 (and_2_out, not_1_out, e2);
  and and_3 (and_3_out, not_1_out, e1, e3);
  and and_4 (and_4_out, e0, not_2_out, not_3_out);
  and and_5 (and_5_out, not_1_out, not_2_out);
  and and_6 (and_6_out, not_1_out, not_3_out, not_4_out);
  and and_7 (and_7_out, not_2_out, not_3_out);
  and and_8 (and_8_out, not_1_out, e2, e3);
  and and_9 (and_9_out, not_2_out, not_3_out);
  and and_10 (and_10_out, not_1_out, e3);
  and and_11 (and_11_out, not_1_out, e1);
  and and_12 (and_12_out, not_1_out, not_2_out, not_4_out);
  and and_13 (and_13_out, not_1_out, not_2_out, e2);
  and and_14 (and_14_out, not_1_out, e2, not_4_out);
  and and_15 (and_15_out, not_1_out, e1, not_3_out, e3);
  and and_16 (and_16_out, e0, not_2_out, not_3_out);
  and and_17 (and_17_out, not_2_out, not_3_out, not_4_out);
  and and_18 (and_18_out, not_1_out, e2, not_4_out);
  and and_19 (and_19_out, not_1_out, not_3_out, not_4_out);
  and and_20 (and_20_out, not_1_out, e1, not_3_out);
  and and_21 (and_21_out, not_1_out, e1, not_4_out);
  and and_22 (and_22_out, e0, not_2_out, not_3_out);
  and and_23 (and_23_out, not_1_out, not_2_out, e2);
  and and_24 (and_24_out, not_1_out, e1, not_3_out);
  and and_25 (and_25_out, not_1_out, e1, not_4_out);
  and and_26 (and_26_out, e0, not_2_out, not_3_out);
  or or_1 (a, and_1_out, and_2_out, and_3_out, and_4_out);
  or or_2 (b, and_5_out, and_6_out, and_7_out, and_8_out);
  or or_3 (c, and_9_out, and_10_out, and_11_out);
  or or_4 (d, and_12_out, and_13_out, and_14_out, and_15_out, and_16_out);
  or or_5 (e, and_17_out, and_18_out);
  or or_6 (f, and_19_out, and_20_out, and_21_out, and_22_out);
  or or_7 (g, and_23_out, and_24_out, and_25_out, and_26_out);
endmodule

module Octet2BCD (
  input  [7:0] E,
  output [3:0] c,
  output [3:0] d,
  output [3:0] u
);

  wire [7:0] divider_1_out;
  wire [7:4] divider_1_rem, divider_2_out, divider_2_rem;

  Divider divider_1 (.a(E), .b(8'ha), .out(divider_1_out), .rem({divider_1_rem, u}));  // open: upper
  Divider divider_2 (.a(divider_1_out), .b(8'ha), .out({divider_2_out, c}), .rem({divider_2_rem, d}));  // open: upper
endmodule

module OctetToBCD (
  input  [7:0] in_1,
  output [3:0] out_2,
  output [3:0] out_3,
  output [3:0] out_4
);

  Octet2BCD octet2bcd_1 (.E(in_1), .c(out_2), .d(out_3), .u(out_4));
endmodule

module OctetToBCD2 (
  input  [7:0] in_1
);

  wire aff7dec_1_a, aff7dec_1_b, aff7dec_1_c, aff7dec_1_d, aff7dec_1_e, aff7dec_1_f, aff7dec_1_g,
       aff7dec_2_a, aff7dec_2_b, aff7dec_2_c, aff7dec_2_d, aff7dec_2_e, aff7dec_2_f, aff7dec_2_g,
       aff7dec_3_a, aff7dec_3_b, aff7dec_3_c, aff7dec_3_d, aff7dec_3_e, aff7dec_3_f, aff7dec_3_g;
  wire [3:0] octettobcd_1_out_2, octettobcd_1_out_3, octettobcd_1_out_4;

  OctetToBCD octettobcd_1 (
    .in_1(in_1), .out_2(octettobcd_1_out_2), .out_3(octettobcd_1_out_3), .out_4(octettobcd_1_out_4));
  aff7dec aff7dec_1 (
    .e0(octettobcd_1_out_2[3]), .e1(octettobcd_1_out_2[1]), .e2(octettobcd_1_out_2[2]),
    .e3(octettobcd_1_out_2[0]), .a(aff7dec_1_a), .b(aff7dec_1_b), .c(aff7dec_1_c), .d(aff7dec_1_d),
    .e(aff7dec_1_e), .f(aff7dec_1_f), .g(aff7dec_1_g));
  aff7dec aff7dec_2 (
    .e0(octettobcd_1_out_3[3]), .e1(octettobcd_1_out_3[1]), .e2(octettobcd_1_out_3[2]),
    .e3(octettobcd_1_out_3[0]), .a(aff7dec_2_a), .b(aff7dec_2_b), .c(aff7dec_2_c), .d(aff7dec_2_d),
    .e(aff7dec_2_e), .f(aff7dec_2_f), .g(aff7dec_2_g));
  aff7dec aff7dec_3 (
    .e0(octettobcd_1_out_4[3]), .e1(octettobcd_1_out_4[2]), .e2(octettobcd_1_out_4[1]),
    .e3(octettobcd_1_out_4[0]), .a(aff7dec_3_a), .b(aff7dec_3_b), .c(aff7dec_3_c), .d(aff7dec_3_d),
    .e(aff7dec_3_e), .f(aff7dec_3_f), .g(aff7dec_3_g));
  _7_Segment_Display u_7_segment_display_1 (
    .g(aff7dec_1_g), .f(aff7dec_1_f), .a(aff7dec_1_a), .b(aff7dec_1_b), .e(aff7dec_1_e), .d(aff7dec_1_d),
    .c(aff7dec_1_c));  // open: dp
  _7_Segment_Display u_7_segment_display_2 (
    .g(aff7dec_2_g), .f(aff7dec_2_f), .a(aff7dec_2_a), .b(aff7dec_2_b), .e(aff7dec_2_e), .d(aff7dec_2_d),
    .c(aff7dec_2_c));  // open: dp
  _7_Segment_Display u_7_segment_display_3 (
    .g(aff7dec_3_g), .f(aff7dec_3_f), .a(aff7dec_3_a), .b(aff7dec_3_b), .e(aff7dec_3_e), .d(aff7dec_3_d),
    .c(aff7dec_3_c));  // open: dp
endmodule

module affichage_ASCII_extend (
  input  in_1
);

  wire aff7hexa_1_a, aff7hexa_1_b, aff7hexa_1_c, aff7hexa_1_d, aff7hexa_1_e, aff7hexa_1_f, aff7hexa_1_g,
       aff7hexa_2_a, aff7hexa_2_b, aff7hexa_2_c, aff7hexa_2_d, aff7hexa_2_e, aff7hexa_2_f, aff7hexa_2_g,
       button_1_out;
  wire [6:0] keyboard_1_data;

  Keyboard keyboard_1 (.clr(button_1_out), .data(keyboard_1_data));  // open: clk, re, avail
  Button button_1 (.out(button_1_out));
  aff7hexa aff7hexa_1 (
    .e0(keyboard_1_data[3]), .e1(keyboard_1_data[2]), .e2(keyboard_1_data[1]), .e3(keyboard_1_data[0]),
    .a(aff7hexa_1_a), .b(aff7hexa_1_b), .c(aff7hexa_1_c), .d(aff7hexa_1_d), .e(aff7hexa_1_e),
    .f(aff7hexa_1_f), .g(aff7hexa_1_g));
  aff7hexa aff7hexa_2 (
    .e0(in_1), .e1(keyboard_1_data[4]), .e2(keyboard_1_data[5]), .e3(keyboard_1_data[6]), .a(aff7hexa_2_a),
    .b(aff7hexa_2_b), .c(aff7hexa_2_c), .d(aff7hexa_2_d), .e(aff7hexa_2_e), .f(aff7hexa_2_f), .g(aff7hexa_2_g));
  _7_Segment_Display u_7_segment_display_1 (
    .g(aff7hexa_1_g), .f(aff7hexa_1_f), .a(aff7hexa_1_a), .b(aff7hexa_1_b), .e(aff7hexa_1_e),
    .d(aff7hexa_1_d), .c(aff7hexa_1_c));  // open: dp
  _7_Segment_Display u_7_segment_display_2 (
    .g(aff7hexa_2_g), .f(aff7hexa_2_f), .a(aff7hexa_2_a), .b(aff7hexa_2_b), .e(aff7hexa_2_e),
    .d(aff7hexa_2_d), .c(aff7hexa_2_c));  // open: dp
endmodule
