// Logisim project tp3.circ as structural Verilog: 11 circuits, main circuit Addionneur_4_bits
module Addionneur_4_bits (
  input  [3:0] A,
  input  [3:0] B,
  output Rout,
  output C3,
  output C2,
  output C1,
  output C0
);

  wire additionneur_complet_1_rout, additionneur_complet_2_rout, additionneur_complet_3_rout;

  Additionneur_complet additionneur_complet_1 (
    .a(A[0]), .b(B[0]), .Rint(1'b0), .Rout(additionneur_complet_1_rout), .S(C0));
  Additionneur_complet additionneur_complet_2 (
    .a(A[1]), .b(B[1]), .Rint(additionneur_complet_1_rout), .Rout(additionneur_complet_2_rout), .S(C1));
  Additionneur_complet additionneur_complet_3 (
    .a(A[2]), .b(B[2]), .Rint(additionneur_complet_2_rout), .Rout(additionneur_complet_3_rout), .S(C2));
  Additionneur_complet additionneur_complet_4 (
    .a(A[3]), .b(B[3]), .Rint(additionneur_complet_3_rout), .Rout(Rout), .S(C3));
endmodule

module demi_additionneur (
  input  a,
  input  b,
  output r,
  output s
);

  wire and_2_out, and_3_out, not_1_out, not_2_out;

  not not_1 (not_1_out, a);
  not not_2 (not_2_out, b);
  and and_1 (r, a, b);
  and and_2 (and_2_out, not_1_out, b);
  and and_3 (and_3_out, a, not_2_out);
  or or_1 (s, and_2_out, and_3_out);
endmodule

module Additionneur_complet (
  input  a,
  input  b,
  input  Rint,
  output Rout,
  output S
);

  wire and_1_out, and_2_out, and_3_out, and_4_out, and_5_out, and_6_out, and_7_out, not_1_out, not_2_out,
       not_3_out;

  not not_1 (not_1_out, a);
  not not_2 (not_2_out, b);
  not not_3 (not_3_out, Rint);
  and and_1 (and_1_out, b, Rint);
  and and_2 (and_2_out, a, Rint);
  and and_3 (and_3_out, a, b);
  and and_4 (and_4_out, not_1_out, not_2_out, Rint);
  and and_5 (and_5_out, not_1_out, b, not_3_out);
  and and_6 (and_6_out, a, not_2_out, not_3_out);
  and and_7 (and_7_out, a, b, Rint);
  or or_1 (Rout, and_1_out, and_2_out, and_3_out);
  or or_2 (S, and_4_out, and_5_out, and_6_out, and_7_out);
endmodule

module main (
  input  [3:0] in_1,
  input  [3:0] in_2
);

  wire addionneur_4_bits_1_c0, addionneur_4_bits_1_c1, addionneur_4_bits_1_c2, addionneur_4_bits_1_c3,
       addionneur_4_bits_1_rout, afficheur_7seg_hexa_1_a, afficheur_7seg_hexa_1_b, afficheur_7seg_hexa_1_c,
       afficheur_7seg_hexa_1_d, afficheur_7seg_hexa_1_e, afficheur_7seg_hexa_1_f, afficheur_7seg_hexa_1_g;

  Addionneur_4_bits addionneur_4_bits_1 (
    .A(in_1), .B(in_2), .Rout(addionneur_4_bits_1_rout), .C3(addionneur_4_bits_1_c3),
    .C2(addionneur_4_bits_1_c2), .C1(addionneur_4_bits_1_c1), .C0(addionneur_4_bits_1_c0));
  afficheur_7seg_hexa afficheur_7seg_hexa_1 (
    .e0(addionneur_4_bits_1_c3), .e1(addionneur_4_bits_1_c2), .e2(addionneur_4_bits_1_c1),
    .e3(addionneur_4_bits_1_c0), .a(afficheur_7seg_hexa_1_a), .b(afficheur_7seg_hexa_1_b),
    .c(afficheur_7seg_hexa_1_c), .d(afficheur_7seg_hexa_1_d), .e(afficheur_7seg_hexa_1_e),
    .f(afficheur_7seg_hexa_1_f), .g(afficheur_7seg_hexa_1_g));
  _7_Segment_Display u_7_segment_display_1 (
    .g(afficheur_7seg_hexa_1_g), .f(afficheur_7seg_hexa_1_f), .a(afficheur_7seg_hexa_1_a),
    .b(afficheur_7seg_hexa_1_b), .e(afficheur_7seg_hexa_1_e), .d(afficheur_7seg_hexa_1_d),
    .c(afficheur_7seg_hexa_1_c), .dp(addionneur_4_bits_1_rout));
endmodule

module afficheur_7seg_hexa (
  input  e0,
  input  e1,
  input  e2,
  input  e3,
  output a,
  output b,
  output c,
  output d,
  output e,
  output f,
  output g
);

  wire and_1_out, and_2_out, and_3_out, and_4_out, and_5_out, and_6_out, and_7_out, and_8_out, and_9_out,
       and_10_out, and_11_out, and_12_out, and_13_out, and_14_out, and_15_out, and_16_out, and_17_out,
       and_18_out, and_19_out, and_20_out, and_21_out, and_22_out, and_23_out, and_24_out, and_25_out,
       and_26_out, and_27_out, and_28_out, and_29_out, and_30_out, and_31_out, and_32_out, and_33_out,
       and_34_out, and_35_out, and_36_out, not_1_out, not_2_out, not_3_out, not_4_out;

  not not_1 (not_1_out, e0);
  not not_2 (not_2_out, e1);
  not not_3 (not_3_out, e2);
  not not_4 (not_4_out, e3);
  and and_1 (and_1_out, not_2_out, not_4_out);
  and and_2 (and_2_out, not_1_out, e2);
  and and_3 (and_3_out, not_1_out, e1, e3);
  and and_4 (and_4_out, e1, e2);
  and and_5 (and_5_out, e0, not_2_out, not_3_out);
  and and_6 (and_6_out, e0, not_4_out);
  and and_7 (and_7_out, not_1_out, not_2_out);
  and and_8 (and_8_out, not_1_out, not_3_out, not_4_out);
  and and_9 (and_9_out, not_2_out, not_4_out);
  and and_10 (and_10_out, not_1_out, e2, e3);
  and and_11 (and_11_out, e0, not_3_out, e3);
  and and_12 (and_12_out, not_1_out, not_3_out);
  and and_13 (and_13_out, not_1_out, e3);
  and and_14 (and_14_out, not_3_out, e3);
  and and_15 (and_15_out, not_1_out, e1);
  and and_16 (and_16_out, e0, not_2_out);
  and and_17 (and_17_out, not_1_out, not_2_out, not_4_out);
  and and_18 (and_18_out, not_1_out, e2, not_4_out);
  and and_19 (and_19_out, not_2_out, e2, e3);
  and and_20 (and_20_out, e1, not_3_out, e3);
  and and_21 (and_21_out, e1, e2, not_4_out);
  and and_22 (and_22_out, e0, not_3_out);
  and and_23 (and_23_out, not_2_out, not_4_out);
  and and_24 (and_24_out, e2, not_4_out);
  and and_25 (and_25_out, e0, e2);
  and and_26 (and_26_out, e0, e1);
  and and_27 (and_27_out, not_3_out, not_4_out);
  and and_28 (and_28_out, not_1_out, e1, not_3_out);
  and and_29 (and_29_out, e1, not_4_out);
  and and_30 (and_30_out, e0, not_2_out);
  and and_31 (and_31_out, e0, e2);
  and and_32 (and_32_out, not_2_out, e2);
  and and_33 (and_33_out, e2, not_4_out);
  and and_34 (and_34_out, not_1_out, e1, not_3_out);
  and and_35 (and_35_out, e0, not_2_out);
  and and_36 (and_36_out, e0, e3);
  or or_1 (a, and_1_out, and_2_out, and_3_out, and_4_out, and_5_out, and_6_out);
  or or_2 (b, and_7_out, and_8_out, and_9_out, and_10_out, and_11_out);
  or or_3 (c, and_12_out, and_13_out, and_14_out, and_15_out, and_16_out);
  or or_4 (d, and_17_out, and_18_out, and_19_out, and_20_out, and_21_out, and_22_out);
  or or_5 (e, and_23_out, and_24_out, and_25_out, and_26_out);
  or or_6 (f, and_27_out, and_28_out, and_29_out, and_30_out, and_31_out);
  or or_7 (g, and_32_out, and_33_out, and_34_out, and_35_out, and_36_out);
endmodule

module additionneur_soustracteur (
  input  [3:0] B,
  input  [3:0] A,
  input  in_3
);

  wire additionneur_complet_1_rout, additionneur_complet_1_s, additionneur_complet_2_rout,
       additionneur_complet_2_s, additionneur_complet_3_rout, additionneur_complet_3_s,
       additionneur_complet_4_rout, additionneur_complet_4_s, afficheur_7seg_hexa_1_a,
       afficheur_7seg_hexa_1_b, afficheur_7seg_hexa_1_c, afficheur_7seg_hexa_1_d, afficheur_7seg_hexa_1_e,
       afficheur_7seg_hexa_1_f, afficheur_7seg_hexa_1_g, xor_1_out, xor_2_out, xor_3_out, xor_4_out;

  xor xor_1 (xor_1_out, in_3, B[3]);
  xor xor_2 (xor_2_out, in_3, B[2]);
  xor xor_3 (xor_3_out, in_3, B[1]);
  xor xor_4 (xor_4_out, in_3, B[0]);
  Additionneur_complet additionneur_complet_1 (
    .a(A[3]), .b(xor_1_out), .Rint(additionneur_complet_2_rout), .Rout(additionneur_complet_1_rout),
    .S(additionneur_complet_1_s));
  Additionneur_complet additionneur_complet_2 (
    .a(A[2]), .b(xor_2_out), .Rint(additionneur_complet_3_rout), .Rout(additionneur_complet_2_rout),
    .S(additionneur_complet_2_s));
  Additionneur_complet additionneur_complet_3 (
    .a(A[1]), .b(xor_3_out), .Rint(additionneur_complet_4_rout), .Rout(additionneur_complet_3_rout),
    .S(additionneur_complet_3_s));
  Additionneur_complet additionneur_complet_4 (
    .a(A[0]), .b(xor_4_out), .Rint(in_3), .Rout(additionneur_complet_4_rout), .S(additionneur_complet_4_s));
  afficheur_7seg_hexa afficheur_7seg_hexa_1 (
    .e0(additionneur_complet_1_s), .e1(additionneur_complet_2_s), .e2(additionneur_complet_3_s),
    .e3(additionneur_complet_4_s), .a(afficheur_7seg_hexa_1_a), .b(afficheur_7seg_hexa_1_b),
    .c(afficheur_7seg_hexa_1_c), .d(afficheur_7seg_hexa_1_d), .e(afficheur_7seg_hexa_1_e),
    .f(afficheur_7seg_hexa_1_f), .g(afficheur_7seg_hexa_1_g));
  _7_Segment_Display u_7_segment_display_1 (
    .g(afficheur_7seg_hexa_1_g), .f(afficheur_7seg_hexa_1_f), .a(afficheur_7seg_hexa_1_a),
    .b(afficheur_7seg_hexa_1_b), .e(afficheur_7seg_hexa_1_e), .d(afficheur_7seg_hexa_1_d),
    .c(afficheur_7seg_hexa_1_c), .dp(additionneur_complet_1_rout));
endmodule

module addionneur_8_bits (
  input  [7:0] A,
  input  [7:0] B
);

  wire addionneur_4_bits_1_rout, afficheur_7seg_deca_1_a, afficheur_7seg_deca_1_b, afficheur_7seg_deca_1_c,
       afficheur_7seg_deca_1_d, afficheur_7seg_deca_1_e, afficheur_7seg_deca_1_f, afficheur_7seg_deca_1_g,
       afficheur_7seg_deca_2_a, afficheur_7seg_deca_2_b, afficheur_7seg_deca_2_c, afficheur_7seg_deca_2_d,
       afficheur_7seg_deca_2_e, afficheur_7seg_deca_2_f, afficheur_7seg_deca_2_g, afficheur_7seg_deca_3_a,
       afficheur_7seg_deca_3_b, afficheur_7seg_deca_3_c, afficheur_7seg_deca_3_d, afficheur_7seg_deca_3_e,
       afficheur_7seg_deca_3_f, afficheur_7seg_deca_3_g;
  wire [3:0] octet2bcd_1_out_2, octet2bcd_1_out_3, octet2bcd_1_out_4;
  wire [7:0] addionneur_4_bits_1_c0;

  Addionneur_4_bits addionneur_4_bits_1 (
    .A(A[3:0]), .B(B[3:0]), .Rout(addionneur_4_bits_1_rout), .C3(addionneur_4_bits_1_c0[3]),
    .C2(addionneur_4_bits_1_c0[2]), .C1(addionneur_4_bits_1_c0[1]), .C0(addionneur_4_bits_1_c0[0]));
  Add_4bits_for_8bits add_4bits_for_8bits_1 (
    .in_1(addionneur_4_bits_1_rout), .A(A[7:4]), .B(B[7:4]), .C3(addionneur_4_bits_1_c0[7]),
    .C2(addionneur_4_bits_1_c0[6]), .C1(addionneur_4_bits_1_c0[5]), .C0(addionneur_4_bits_1_c0[4]));  // open: Rout
  Octet2BCD octet2bcd_1 (
    .in_1(addionneur_4_bits_1_c0), .out_2(octet2bcd_1_out_2), .out_3(octet2bcd_1_out_3),
    .out_4(octet2bcd_1_out_4));
  afficheur_7seg_deca afficheur_7seg_deca_1 (
    .e0(octet2bcd_1_out_2[0]), .e1(octet2bcd_1_out_2[1]), .e2(octet2bcd_1_out_2[2]),
    .e3(octet2bcd_1_out_2[3]), .a(afficheur_7seg_deca_1_a), .b(afficheur_7seg_deca_1_b),
    .c(afficheur_7seg_deca_1_c), .d(afficheur_7seg_deca_1_d), .e(afficheur_7seg_deca_1_e),
    .f(afficheur_7seg_deca_1_f), .g(afficheur_7seg_deca_1_g));
  afficheur_7seg_deca afficheur_7seg_deca_2 (
    .e0(octet2bcd_1_out_4[0]), .e1(octet2bcd_1_out_4[1]), .e2(octet2bcd_1_out_4[2]),
    .e3(octet2bcd_1_out_4[3]), .a(afficheur_7seg_deca_2_a), .b(afficheur_7seg_deca_2_b),
    .c(afficheur_7seg_deca_2_c), .d(afficheur_7seg_deca_2_d), .e(afficheur_7seg_deca_2_e),
    .f(afficheur_7seg_deca_2_f), .g(afficheur_7seg_deca_2_g));
  _7_Segment_Display u_7_segment_display_1 (
    .g(afficheur_7seg_deca_1_g), .f(afficheur_7seg_deca_1_f), .a(afficheur_7seg_deca_1_a),
    .b(afficheur_7seg_deca_1_b), .e(afficheur_7seg_deca_1_e), .d(afficheur_7seg_deca_1_d),
    .c(afficheur_7seg_deca_1_c));  // open: dp
  afficheur_7seg_deca afficheur_7seg_deca_3 (
    .e0(octet2bcd_1_out_3[0]), .e1(octet2bcd_1_out_3[1]), .e2(octet2bcd_1_out_3[2]),
    .e3(octet2bcd_1_out_3[3]), .a(afficheur_7seg_deca_3_a), .b(afficheur_7seg_deca_3_b),
    .c(afficheur_7seg_deca_3_c), .d(afficheur_7seg_deca_3_d), .e(afficheur_7seg_deca_3_e),
    .f(afficheur_7seg_deca_3_f), .g(afficheur_7seg_deca_3_g));
  _7_Segment_Display u_7_segment_display_2 (
    .g(afficheur_7seg_deca_3_g), .f(afficheur_7seg_deca_3_f), .a(afficheur_7seg_deca_3_a),
    .b(afficheur_7seg_deca_3_b), .e(afficheur_7seg_deca_3_e), .d(afficheur_7seg_deca_3_d),
    .c(afficheur_7seg_deca_3_c));  // open: dp
  _7_Segment_Display u_7_segment_display_3 (
    .g(afficheur_7seg_deca_2_g), .f(afficheur_7seg_deca_2_f), .a(afficheur_7seg_deca_2_a),
    .b(afficheur_7seg_deca_2_b), .e(afficheur_7seg_deca_2_e), .d(afficheur_7seg_deca_2_d),
    .c(afficheur_7seg_deca_2_c));  // open: dp
endmodule

module Add_4bits_for_8bits (
  input  in_1,
  input  [3:0] A,
  input  [3:0] B,
  output Rout,
  output C3,
  output C2,
  output C1,
  output C0
);

  wire additionneur_complet_1_rout, additionneur_complet_2_rout, additionneur_complet_3_rout;

  Additionneur_complet additionneur_complet_1 (
    .a(A[0]), .b(B[0]), .Rint(in_1), .Rout(additionneur_complet_1_rout), .S(C0));
  Additionneur_complet additionneur_complet_2 (
    .a(A[1]), .b(B[1]), .Rint(additionneur_complet_1_rout), .Rout(additionneur_complet_2_rout), .S(C1));
  Additionneur_complet additionneur_complet_3 (
    .a(A[2]), .b(B[2]), .Rint(additionneur_complet_2_rout), .Rout(additionneur_complet_3_rout), .S(C2));
  Additionneur_complet additionneur_complet_4 (
    .a(A[3]), .b(B[3]), .Rint(additionneur_complet_3_rout), .Rout(Rout), .S(C3));
endmodule

module Octet_2_BCD_Base (
  input  [7:0] E,
  output [3:0] c,
  output [3:0] d,
  output [3:0] u
);

  wire [7:0] divider_1_out;
  wire [7:4] divider_1_rem, divider_2_out, divider_2_rem;

  Divider divider_1 (.a(E), .b(8'ha), .out(divider_1_out), .rem({divider_1_rem, u}));  // open: upper
  Divider divider_2 (.a(divider_1_out), .b(8'ha), .out({divider_2_out, c}), .rem({divider_2_rem, d}));  // open: upper
endmodule

module Octet2BCD (
  input  [7:0] in_1,
  output [3:0] out_2,
  output [3:0] out_3,
  output [3:0] out_4
);

  Octet_2_BCD_Base octet_2_bcd_base_1 (.E(in_1), .c(out_2), .d(out_3), .u(out_4));
endmodule

module afficheur_7seg_deca (
  input  e0,
  input  e1,
  input  e2,
  input  e3,
  output a,
  output b,
  output c,
  output d,
  output e,
  output f,
  output g
);

  wire and_1_out, and_2_out, and_3_out, and_4_out, and_5_out, and_6_out, and_7_out, and_8_out, and_9_out,
       and_10_out, and_11_out, and_12_out, and_13_out, and_14_out, and_15_out, and_16_out, and_17_out,
       and_18_out, and_19_out, and_20_out, and_21_out, and_22_out, and_23_out, and_24_out, and_25_out,
       and_26_out, not_1_out, not_2_out, not_3_out, not_4_out;

  not not_1 (not_1_out, e0);
  not not_2 (not_2_out, e1);
  not not_3 (not_3_out, e2);
  not not_4 (not_4_out, e3);
  and and_1 (and_1_out, not_1_out, not_2_out, not_4_out);
  and and_2 (and_2_out, not_1_out, e2);
  and and_3 (and_3_out, not_1_out, e1, e3);
  and and_4 (and_4_out, e0, not_2_out, not_3_out);
  and and_5 (and_5_out, not_1_out, not_2_out);
  and and_6 (and_6_out, not_1_out, not_3_out, not_4_out);
  and and_7 (and_7_out, not_2_out, not_3_out);
  and and_8 (and_8_out, not_1_out, e2, e3);
  and and_9 (and_9_out, not_2_out, not_3_out);
  and and_10 (and_10_out, not_1_out, e3);
  and and_11 (and_11_out, not_1_out, e1);
  and and_12 (and_12_out, not_1_out, not_2_out, not_4_out);
  and and_13 (and_13_out, not_1_out, not_2_out, e2);
  and and_14 (and_14_out, not_1_out, e2, not_4_out);
  and and_15 (and_15_out, not_1_out, e1, not_3_out, e3);
  and and_16 (and_16_out, e0, not_2_out, not_3_out);
  and and_17 (and_17_out, not_2_out, not_3_out, not_4_out);
  and and_18 (and_18_out, not_1_out, e2, not_4_out);
  and and_19 (and_19_out, not_1_out, not_3_out, not_4_out);
  and and_20 (and_20_out, not_1_out, e1, not_3_out);
  and and_21 (and_21_out, not_1_out, e1, not_4_out);
  and and_22 (and_22_out, e0, not_2_out, not_3_out);
  and and_23 (and_23_out, not_1_out, not_2_out, e2);
  and and_24 (and_24_out, not_1_out, e1, not_3_out);
  and and_25 (and_25_out, not_1_out, e1, not_4_out);
  and and_26 (and_26_out, e0, not_2_out, not_3_out);
  or or_1 (a, and_1_out, and_2_out, and_3_out, and_4_out);
  or or_2 (b, and_5_out, and_6_out, and_7_out, and_8_out);
  or or_3 (c, and_9_out, and_10_out, and_11_out);
  or or_4 (d, and_12_out, and_13_out, and_14_out, and_15_out, and_16_out);
  or or_5 (e, and_17_out, and_18_out);
  or or_6 (f, and_19_out, and_20_out, and_21_out, and_22_out);
  or or_7 (g, and_23_out, and_24_out, and_25_out, and_26_out);
endmodule
