// Logisim project tp4.circ as structural Verilog
module decodeur_2_entres (
  input  e0,
  input  e1,
  output s0,
  output s1,
  output s2,
  output s3
);

  wire not_1_out, not_2_out;

  not not_1 (not_1_out, e0);
  not not_2 (not_2_out, e1);
  and and_1 (s0, e0, e1);
  and and_2 (s1, e0, not_2_out);
  and and_3 (s2, not_1_out, e1);
  and and_4 (s3, not_1_out, not_2_out);
endmodule

module multiplexeur_4_entres_4bits (
  input  [3:0] e0,
  input  [3:0] e1,
  input  [3:0] e2,
  input  [3:0] e3,
  input  a0,
  input  a1,
  output [3:0] out_7
);

  wire decodeur_2_entres_1_s0, decodeur_2_entres_1_s1, decodeur_2_entres_1_s2, decodeur_2_entres_1_s3;
  wire [3:0] buffer_1_out, controlled_buffer_1_out, controlled_buffer_3_out;

  decodeur_2_entres decodeur_2_entres_1 (
    .e0(a0), .e1(a1), .s0(decodeur_2_entres_1_s0), .s1(decodeur_2_entres_1_s1), .s2(decodeur_2_entres_1_s2),
    .s3(decodeur_2_entres_1_s3));
  assign controlled_buffer_1_out = decodeur_2_entres_1_s3 ? e0 : 4'bz;  // Controlled_Buffer controlled_buffer_1
  assign controlled_buffer_1_out = decodeur_2_entres_1_s2 ? e1 : 4'bz;  // Controlled_Buffer controlled_buffer_2
  assign controlled_buffer_3_out = decodeur_2_entres_1_s1 ? e2 : 4'bz;  // Controlled_Buffer controlled_buffer_3
  assign controlled_buffer_3_out = decodeur_2_entres_1_s0 ? e3 : 4'bz;  // Controlled_Buffer controlled_buffer_4
  assign buffer_1_out = controlled_buffer_1_out;  // Buffer buffer_1, 4 bits wide
  assign buffer_1_out = controlled_buffer_3_out;  // Buffer buffer_2, 4 bits wide
  assign out_7 = buffer_1_out;  // Buffer buffer_3, 4 bits wide
endmodule

module unite_arithmetique_1bit (
  input  a,
  input  b,
  input  c_in,
  input  a0,
  input  a1,
  output f,
  output cou_out
);

  wire additionneur_complet_1_s, and_1_out, not_1_out, or_1_out;

  not not_1 (not_1_out, a);
  or or_1 (or_1_out, a, b);
  and and_1 (and_1_out, b, a);
  additionneur_complet additionneur_complet_1 (.a(a), .b(b), .Rint(c_in), .Rout(cou_out), .S(additionneur_complet_1_s));
  multiplexeur_4entres_1bit multiplexeur_4entres_1bit_1 (
    .e0(not_1_out), .e1(or_1_out), .e2(and_1_out), .e3(additionneur_complet_1_s), .a0(a0), .a1(a1), .out_7(f));
endmodule

module multiplexeur_4entres_1bit (
  input  e0,
  input  e1,
  input  e2,
  input  e3,
  input  a0,
  input  a1,
  output out_7
);

  wire buffer_1_out, controlled_buffer_1_out, controlled_buffer_3_out, decodeur_2_entres_1_s0,
       decodeur_2_entres_1_s1, decodeur_2_entres_1_s2, decodeur_2_entres_1_s3;

  decodeur_2_entres decodeur_2_entres_1 (
    .e0(a0), .e1(a1), .s0(decodeur_2_entres_1_s0), .s1(decodeur_2_entres_1_s1), .s2(decodeur_2_entres_1_s2),
    .s3(decodeur_2_entres_1_s3));
  assign controlled_buffer_1_out = decodeur_2_entres_1_s3 ? e0 : 1'bz;  // Controlled_Buffer controlled_buffer_1
  assign controlled_buffer_1_out = decodeur_2_entres_1_s2 ? e1 : 1'bz;  // Controlled_Buffer controlled_buffer_2
  assign controlled_buffer_3_out = decodeur_2_entres_1_s1 ? e2 : 1'bz;  // Controlled_Buffer controlled_buffer_3
  assign controlled_buffer_3_out = decodeur_2_entres_1_s0 ? e3 : 1'bz;  // Controlled_Buffer controlled_buffer_4
  buf buffer_1 (buffer_1_out, controlled_buffer_1_out);
  buf buffer_2 (buffer_1_out, controlled_buffer_3_out);
  buf buffer_3 (out_7, buffer_1_out);
endmodule

module additionneur_complet (
  input  a,
  input  b,
  input  Rint,
  output Rout,
  output S
);

  wire and_1_out, and_2_out, and_3_out, and_4_out, and_5_out, and_6_out, and_7_out, not_1_out, not_2_out,
       not_3_out;

  not not_1 (not_1_out, a);
  not not_2 (not_2_out, b);
  not not_3 (not_3_out, Rint);
  and and_1 (and_1_out, b, Rint);
  and and_2 (and_2_out, a, Rint);
  and and_3 (and_3_out, a, b);
  and and_4 (and_4_out, not_1_out, not_2_out, Rint);
  and and_5 (and_5_out, not_1_out, b, not_3_out);
  and and_6 (and_6_out, a, not_2_out, not_3_out);
  and and_7 (and_7_out, a, b, Rint);
  or or_1 (Rout, and_1_out, and_2_out, and_3_out);
  or or_2 (S, and_4_out, and_5_out, and_6_out, and_7_out);
endmodule

module unite_arithmetique_4bits (
  input  [3:0] a,
  input  c_in,
  input  [3:0] b,
  input  a0,
  input  a1,
  output f0,
  output f1,
  output f2,
  output f3,
  output cou_out
);

  wire unite_arithmetique_1bit_1_cou_out, unite_arithmetique_1bit_2_cou_out,
       unite_arithmetique_1bit_3_cou_out;

  unite_arithmetique_1bit unite_arithmetique_1bit_1 (
    .a(a[0]), .b(b[0]), .c_in(c_in), .a0(a0), .a1(a1), .f(f0), .cou_out(unite_arithmetique_1bit_1_cou_out));
  unite_arithmetique_1bit unite_arithmetique_1bit_2 (
    .a(a[1]), .b(b[1]), .c_in(unite_arithmetique_1bit_1_cou_out), .a0(a0), .a1(a1), .f(f1),
    .cou_out(unite_arithmetique_1bit_2_cou_out));
  unite_arithmetique_1bit unite_arithmetique_1bit_3 (
    .a(a[2]), .b(b[2]), .c_in(unite_arithmetique_1bit_2_cou_out), .a0(a0), .a1(a1), .f(f2),
    .cou_out(unite_arithmetique_1bit_3_cou_out));
  unite_arithmetique_1bit unite_arithmetique_1bit_4 (
    .a(a[3]), .b(b[3]), .c_in(unite_arithmetique_1bit_3_cou_out), .a0(a0), .a1(a1), .f(f3), .cou_out(cou_out));
endmodule

module additionneur_complet_4bits (
  input  [3:0] A,
  input  [3:0] B,
  output Rout,
  output C3,
  output C2,
  output C1,
  output C0
);

  wire additionneur_complet_1_rout, additionneur_complet_2_rout, additionneur_complet_3_rout;

  additionneur_complet additionneur_complet_1 (
    .a(A[0]), .b(B[0]), .Rint(1'b0), .Rout(additionneur_complet_1_rout), .S(C0));
  additionneur_complet additionneur_complet_2 (
    .a(A[1]), .b(B[1]), .Rint(additionneur_complet_1_rout), .Rout(additionneur_complet_2_rout), .S(C1));
  additionneur_complet additionneur_complet_3 (
    .a(A[2]), .b(B[2]), .Rint(additionneur_complet_2_rout), .Rout(additionneur_complet_3_rout), .S(C2));
  additionneur_complet additionneur_complet_4 (
    .a(A[3]), .b(B[3]), .Rint(additionneur_complet_3_rout), .Rout(Rout), .S(C3));
endmodule
