// Logisim project tp5.circ as structural Verilog: 4 circuits, main circuit main
module main (
  output out_1,
  output out_2,
  output out_3,
  output out_4
);

  Clock clock_1 (.out(out_1));
  Clock #(.highDuration(2)) clock_2 (.out(out_2));
  Clock #(.highDuration(3)) clock_3 (.out(out_3));
  Clock #(.highDuration(4)) clock_4 (.out(out_4));
endmodule

module decalage_gauche (
  input  [3:0] e,
  output [3:0] S
);

  wire clock_1_out, clock_2_out, clock_3_out, clock_4_out;

  T_Flip_Flop t_ff_1 (.T(e[0]), .clk(clock_1_out), .Q(S[3]));  // open: Qn, reset, preset
  Clock #(.lowDuration(4)) clock_1 (.out(clock_1_out));
  Clock #(.highDuration(2), .lowDuration(3)) clock_2 (.out(clock_2_out));
  T_Flip_Flop t_ff_2 (.T(e[1]), .clk(clock_2_out), .Q(S[2]));  // open: Qn, reset, preset
  Clock #(.highDuration(3), .lowDuration(2)) clock_3 (.out(clock_3_out));
  T_Flip_Flop t_ff_3 (.T(e[2]), .clk(clock_3_out), .Q(S[1]));  // open: Qn, reset, preset
  Clock #(.highDuration(4)) clock_4 (.out(clock_4_out));
  T_Flip_Flop t_ff_4 (.T(e[3]), .clk(clock_4_out), .Q(S[0]));  // open: Qn, reset, preset
endmodule

module decalage_droite (
  input  [3:0] e1,
  output [3:0] S1
);

  wire clock_1_out, clock_2_out, clock_3_out, clock_4_out;

  T_Flip_Flop t_ff_1 (.T(e1[0]), .clk(clock_1_out), .Q(S1[0]));  // open: Qn, reset, preset
  Clock #(.lowDuration(4)) clock_1 (.out(clock_1_out));
  T_Flip_Flop t_ff_2 (.T(e1[1]), .clk(clock_2_out), .Q(S1[1]));  // open: Qn, reset, preset
  Clock #(.highDuration(2), .lowDuration(3)) clock_2 (.out(clock_2_out));
  T_Flip_Flop t_ff_3 (.T(e1[2]), .clk(clock_3_out), .Q(S1[2]));  // open: Qn, reset, preset
  Clock #(.highDuration(3), .lowDuration(2)) clock_3 (.out(clock_3_out));
  T_Flip_Flop t_ff_4 (.T(e1[3]), .clk(clock_4_out), .Q(S1[3]));  // open: Qn, reset, preset
  Clock #(.highDuration(4)) clock_4 (.out(clock_4_out));
endmodule

module decalage_G_D (
  input  in_1,
  output [3:0] decalage_gauche,
  output [3:0] decalage_droite
);

  wire clock_1_out, clock_2_out, clock_3_out, clock_4_out, clock_5_out, clock_6_out, clock_7_out,
       clock_8_out, not_1_out;

  not not_1 (not_1_out, in_1);
  T_Flip_Flop t_ff_1 (.T(not_1_out), .clk(clock_1_out), .Q(decalage_droite[3]));  // open: Qn, reset, preset
  Clock #(.lowDuration(4)) clock_1 (.out(clock_1_out));
  T_Flip_Flop t_ff_2 (.T(not_1_out), .clk(clock_2_out), .Q(decalage_droite[2]));  // open: Qn, reset, preset
  Clock #(.highDuration(2), .lowDuration(3)) clock_2 (.out(clock_2_out));
  T_Flip_Flop t_ff_3 (.T(in_1), .clk(clock_3_out), .Q(decalage_gauche[0]));  // open: Qn, reset, preset
  Clock #(.lowDuration(4)) clock_3 (.out(clock_3_out));
  T_Flip_Flop t_ff_4 (.T(not_1_out), .clk(clock_4_out), .Q(decalage_droite[1]));  // open: Qn, reset, preset
  Clock #(.highDuration(3), .lowDuration(2)) clock_4 (.out(clock_4_out));
  T_Flip_Flop t_ff_5 (.T(in_1), .clk(clock_5_out), .Q(decalage_gauche[1]));  // open: Qn, reset, preset
  Clock #(.highDuration(2), .lowDuration(3)) clock_5 (.out(clock_5_out));
  T_Flip_Flop t_ff_6 (.T(not_1_out), .clk(clock_6_out), .Q(decalage_droite[0]));  // open: Qn, reset, preset
  Clock #(.highDuration(4)) clock_6 (.out(clock_6_out));
  T_Flip_Flop t_ff_7 (.T(in_1), .clk(clock_7_out), .Q(decalage_gauche[2]));  // open: Qn, reset, preset
  Clock #(.highDuration(3), .lowDuration(2)) clock_7 (.out(clock_7_out));
  T_Flip_Flop t_ff_8 (.T(in_1), .clk(clock_8_out), .Q(decalage_gauche[3]));  // open: Qn, reset, preset
  Clock #(.highDuration(4)) clock_8 (.out(clock_8_out));
endmodule
