// Logisim project tp6.circ as structural Verilog: 4 circuits, main circuit registre_4bits
module registre_4bits (
  input  [3:0] e,
  input  EN,
  input  Write,
  input  Read,
  output [3:0] out_5
);

  registre_1bit registre_1bit_1 (.e(e[3]), .EN(EN), .Write(Write), .Read(Read), .s(out_5[3]));
  registre_1bit registre_1bit_2 (.e(e[2]), .EN(EN), .Write(Write), .Read(Read), .s(out_5[2]));
  registre_1bit registre_1bit_3 (.e(e[1]), .EN(EN), .Write(Write), .Read(Read), .s(out_5[1]));
  registre_1bit registre_1bit_4 (.e(e[0]), .EN(EN), .Write(Write), .Read(Read), .s(out_5[0]));
endmodule

module registre_1bit (
  input  e,
  input  EN,
  input  Write,
  input  Read,
  output s
);

  wire and_1_out, and_2_out, d_ff_1_q;

  D_Flip_Flop d_ff_1 (.D(e), .clk(and_1_out), .Q(d_ff_1_q));  // open: Qn, preset, reset
  and and_1 (and_1_out, EN, Write);
  and and_2 (and_2_out, EN, Read);
  assign s = and_2_out ? d_ff_1_q : 1'bz;  // Controlled_Buffer controlled_buffer_1
endmodule

module decodeur (
  input  e0,
  input  e1,
  input  e2,
  output s0,
  output s1,
  output s2,
  output s3,
  output s4,
  output s5,
  output s6,
  output s7
);

  wire i0_out, i1_out, i2_out;

  not i0 (i0_out, e0);
  not i1 (i1_out, e2);
  not i2 (i2_out, e1);
  and and_1 (s0, i0_out, i1_out, i2_out);
  and and_2 (s1, e0, i2_out, i1_out);
  and and_3 (s2, e1, i1_out, i0_out);
  and and_4 (s3, i1_out, e1, e0);
  and and_5 (s4, i0_out, i2_out, e2);
  and and_6 (s5, e0, i2_out, e2);
  and and_7 (s6, i0_out, e1, e2);
  and and_8 (s7, e0, e1, e2);
endmodule

module main (
  input  in_1,
  input  in_2,
  input  in_3,
  input  [3:0] mot,
  input  Write,
  input  Read,
  output [3:0] out_7
);

  wire and_1_out, and_2_out, and_3_out, and_4_out, and_5_out, and_6_out, and_7_out, and_8_out, and_9_out,
       and_10_out, and_11_out, and_12_out, and_13_out, and_14_out, and_15_out, and_16_out, decodeur_1_s0,
       decodeur_1_s1, decodeur_1_s2, decodeur_1_s3, decodeur_1_s4, decodeur_1_s5, decodeur_1_s6,
       decodeur_1_s7;
  wire [3:0] buffer_1_out, buffer_2_out, controlled_buffer_1_out, controlled_buffer_2_out,
       controlled_buffer_5_out, controlled_buffer_7_out, registre1_out_5, registre2_out_5, registre3_out_5,
       registre4_out_5, registre5_out_5, registre6_out_5, registre7_out_5, registre_0_out_5;

  decodeur decodeur_1 (
    .e0(in_1), .e1(in_2), .e2(in_3), .s0(decodeur_1_s0), .s1(decodeur_1_s1), .s2(decodeur_1_s2),
    .s3(decodeur_1_s3), .s4(decodeur_1_s4), .s5(decodeur_1_s5), .s6(decodeur_1_s6), .s7(decodeur_1_s7));
  and and_1 (and_1_out, decodeur_1_s0, Write);
  and and_2 (and_2_out, decodeur_1_s1, Write);
  and and_3 (and_3_out, decodeur_1_s2, Write);
  and and_4 (and_4_out, decodeur_1_s3, Write);
  and and_5 (and_5_out, decodeur_1_s6, Write);
  and and_6 (and_6_out, decodeur_1_s7, Write);
  and and_7 (and_7_out, decodeur_1_s0, Read);
  and and_8 (and_8_out, decodeur_1_s1, Read);
  and and_9 (and_9_out, decodeur_1_s2, Read);
  and and_10 (and_10_out, decodeur_1_s3, Read);
  and and_11 (and_11_out, decodeur_1_s4, Write);
  and and_12 (and_12_out, decodeur_1_s5, Write);
  and and_13 (and_13_out, decodeur_1_s6, Read);
  and and_14 (and_14_out, decodeur_1_s7, Read);
  and and_15 (and_15_out, decodeur_1_s4, Read);
  and and_16 (and_16_out, decodeur_1_s5, Read);
  assign controlled_buffer_1_out = and_7_out ? registre_0_out_5 : 4'bz;  // Controlled_Buffer controlled_buffer_1
  registre_4bits registre_0 (
    .e(mot), .EN(decodeur_1_s0), .Write(and_1_out), .Read(and_7_out), .out_5(registre_0_out_5));
  registre_4bits registre1 (.e(mot), .EN(decodeur_1_s1), .Write(and_2_out), .Read(and_8_out), .out_5(registre1_out_5));
  assign controlled_buffer_2_out = and_9_out ? registre2_out_5 : 4'bz;  // Controlled_Buffer controlled_buffer_2
  registre_4bits registre2 (.e(mot), .EN(decodeur_1_s2), .Write(and_3_out), .Read(and_9_out), .out_5(registre2_out_5));
  assign controlled_buffer_2_out = and_10_out ? registre3_out_5 : 4'bz;  // Controlled_Buffer controlled_buffer_3
  registre_4bits registre3 (.e(mot), .EN(decodeur_1_s3), .Write(and_4_out), .Read(and_10_out), .out_5(registre3_out_5));
  assign controlled_buffer_1_out = and_8_out ? registre1_out_5 : 4'bz;  // Controlled_Buffer controlled_buffer_4
  registre_4bits registre4 (
    .e(mot), .EN(decodeur_1_s4), .Write(and_11_out), .Read(and_15_out), .out_5(registre4_out_5));
  registre_4bits registre5 (
    .e(mot), .EN(decodeur_1_s5), .Write(and_12_out), .Read(and_16_out), .out_5(registre5_out_5));
  registre_4bits registre6 (.e(mot), .EN(decodeur_1_s6), .Write(and_5_out), .Read(and_13_out), .out_5(registre6_out_5));
  registre_4bits registre7 (.e(mot), .EN(decodeur_1_s7), .Write(and_6_out), .Read(and_14_out), .out_5(registre7_out_5));
  assign buffer_1_out = controlled_buffer_1_out;  // Buffer buffer_1, 4 bits wide
  assign buffer_2_out = buffer_1_out;  // Buffer buffer_2, 4 bits wide
  assign buffer_1_out = controlled_buffer_2_out;  // Buffer buffer_3, 4 bits wide
  assign controlled_buffer_5_out = and_15_out ? registre4_out_5 : 4'bz;  // Controlled_Buffer controlled_buffer_5
  assign controlled_buffer_5_out = and_16_out ? registre5_out_5 : 4'bz;  // Controlled_Buffer controlled_buffer_6
  assign controlled_buffer_7_out = and_13_out ? registre6_out_5 : 4'bz;  // Controlled_Buffer controlled_buffer_7
  assign controlled_buffer_7_out = and_14_out ? registre7_out_5 : 4'bz;  // Controlled_Buffer controlled_buffer_8
  assign buffer_2_out = controlled_buffer_7_out;  // Buffer buffer_4, 4 bits wide
  assign buffer_2_out = controlled_buffer_5_out;  // Buffer buffer_5, 4 bits wide
  assign out_7 = buffer_2_out;  // Buffer buffer_6, 4 bits wide
endmodule
