// Logisim project tp7.circ as structural Verilog: 7 circuits, main circuit compteur_synchrone
module compteur_synchrone (
);

  wire and_1_out, and_2_out, clock_1_out, j_k_ff_1_q, j_k_ff_2_q, j_k_ff_3_q;

  Clock clock_1 (.out(clock_1_out));
  J_K_Flip_Flop #(.trigger("falling")) j_k_ff_1 (
    .J(1'b1), .K(1'b1), .clk(clock_1_out), .Q(j_k_ff_1_q));  // open: Qn, preset, reset
  J_K_Flip_Flop #(.trigger("falling")) j_k_ff_2 (
    .J(j_k_ff_1_q), .K(j_k_ff_1_q), .clk(clock_1_out), .Q(j_k_ff_2_q));  // open: Qn, preset, reset
  and and_1 (and_1_out, j_k_ff_1_q, j_k_ff_2_q);
  J_K_Flip_Flop #(.trigger("falling")) j_k_ff_3 (
    .J(and_1_out), .K(and_1_out), .clk(clock_1_out), .Q(j_k_ff_3_q));  // open: Qn, preset, reset
  and and_2 (and_2_out, and_1_out, j_k_ff_3_q);
  J_K_Flip_Flop #(.trigger("falling")) j_k_ff_4 (
    .J(and_2_out), .K(and_2_out), .clk(clock_1_out));  // open: Q, Qn, preset, reset
endmodule

module compteur_asynchrone (
);

  wire afficheur_hexa_1_a, afficheur_hexa_1_b, afficheur_hexa_1_c, afficheur_hexa_1_d, afficheur_hexa_1_e,
       afficheur_hexa_1_f, afficheur_hexa_1_g, and_1_out, clock_1_out, j_k_ff_1_q, j_k_ff_2_q, j_k_ff_3_q,
       j_k_ff_4_q;

  J_K_Flip_Flop #(.trigger("falling")) j_k_ff_1 (
    .J(1'b1), .K(1'b1), .clk(clock_1_out), .Q(j_k_ff_1_q));  // open: Qn, preset, reset
  Clock clock_1 (.out(clock_1_out));
  J_K_Flip_Flop #(.trigger("falling")) j_k_ff_2 (
    .J(1'b1), .K(1'b1), .clk(j_k_ff_1_q), .Q(j_k_ff_2_q));  // open: Qn, preset, reset
  and and_1 (and_1_out, j_k_ff_1_q, j_k_ff_2_q);
  J_K_Flip_Flop #(.trigger("falling")) j_k_ff_3 (
    .J(1'b1), .K(1'b1), .clk(and_1_out), .Q(j_k_ff_3_q));  // open: Qn, preset, reset
  afficheur_hexa afficheur_hexa_1 (
    .e0(j_k_ff_4_q), .e1(j_k_ff_3_q), .e2(j_k_ff_2_q), .e3(j_k_ff_1_q), .a(afficheur_hexa_1_a),
    .b(afficheur_hexa_1_b), .c(afficheur_hexa_1_c), .d(afficheur_hexa_1_d), .e(afficheur_hexa_1_e),
    .f(afficheur_hexa_1_f), .g(afficheur_hexa_1_g));
  J_K_Flip_Flop #(.trigger("falling")) j_k_ff_4 (
    .J(1'b1), .K(1'b1), .clk(j_k_ff_3_q), .Q(j_k_ff_4_q));  // open: Qn, preset, reset
  _7_Segment_Display u_7_segment_display_1 (
    .g(afficheur_hexa_1_g), .f(afficheur_hexa_1_f), .a(afficheur_hexa_1_a), .b(afficheur_hexa_1_b),
    .e(afficheur_hexa_1_e), .d(afficheur_hexa_1_d), .c(afficheur_hexa_1_c));  // open: dp
endmodule

module compteur_asynchrone_0_9 (
);

  wire afficheur_hexa_1_a, afficheur_hexa_1_b, afficheur_hexa_1_c, afficheur_hexa_1_d, afficheur_hexa_1_e,
       afficheur_hexa_1_f, afficheur_hexa_1_g, and_1_out, and_2_out, clock_1_out, j_k_ff_1_q, j_k_ff_2_q,
       j_k_ff_3_q, j_k_ff_4_q;

  J_K_Flip_Flop #(.trigger("falling")) j_k_ff_1 (
    .J(1'b1), .K(1'b1), .clk(clock_1_out), .Q(j_k_ff_1_q), .reset(and_1_out));  // open: Qn, preset
  Clock clock_1 (.out(clock_1_out));
  and and_1 (and_1_out, j_k_ff_2_q, j_k_ff_4_q);
  J_K_Flip_Flop #(.trigger("falling")) j_k_ff_2 (
    .J(1'b1), .K(1'b1), .clk(j_k_ff_1_q), .Q(j_k_ff_2_q), .reset(and_1_out));  // open: Qn, preset
  and and_2 (and_2_out, j_k_ff_1_q, j_k_ff_2_q);
  J_K_Flip_Flop #(.trigger("falling")) j_k_ff_3 (
    .J(1'b1), .K(1'b1), .clk(and_2_out), .Q(j_k_ff_3_q), .reset(and_1_out));  // open: Qn, preset
  afficheur_hexa afficheur_hexa_1 (
    .e0(j_k_ff_4_q), .e1(j_k_ff_3_q), .e2(j_k_ff_2_q), .e3(j_k_ff_1_q), .a(afficheur_hexa_1_a),
    .b(afficheur_hexa_1_b), .c(afficheur_hexa_1_c), .d(afficheur_hexa_1_d), .e(afficheur_hexa_1_e),
    .f(afficheur_hexa_1_f), .g(afficheur_hexa_1_g));
  J_K_Flip_Flop #(.trigger("falling")) j_k_ff_4 (
    .J(1'b1), .K(1'b1), .clk(j_k_ff_3_q), .Q(j_k_ff_4_q), .reset(and_1_out));  // open: Qn, preset
  _7_Segment_Display u_7_segment_display_1 (
    .g(afficheur_hexa_1_g), .f(afficheur_hexa_1_f), .a(afficheur_hexa_1_a), .b(afficheur_hexa_1_b),
    .e(afficheur_hexa_1_e), .d(afficheur_hexa_1_d), .c(afficheur_hexa_1_c));  // open: dp
endmodule

module afficheur_hexa (
  input  e0,
  input  e1,
  input  e2,
  input  e3,
  output a,
  output b,
  output c,
  output d,
  output e,
  output f,
  output g
);

  wire and_1_out, and_2_out, and_3_out, and_4_out, and_5_out, and_6_out, and_7_out, and_8_out, and_9_out,
       and_10_out, and_11_out, and_12_out, and_13_out, and_14_out, and_15_out, and_16_out, and_17_out,
       and_18_out, and_19_out, and_20_out, and_21_out, and_22_out, and_23_out, and_24_out, and_25_out,
       and_26_out, and_27_out, and_28_out, and_29_out, and_30_out, and_31_out, and_32_out, and_33_out,
       and_34_out, and_35_out, and_36_out, not_1_out, not_2_out, not_3_out, not_4_out;

  not not_1 (not_1_out, e0);
  not not_2 (not_2_out, e1);
  not not_3 (not_3_out, e2);
  not not_4 (not_4_out, e3);
  and and_1 (and_1_out, not_2_out, not_4_out);
  and and_2 (and_2_out, not_1_out, e2);
  and and_3 (and_3_out, not_1_out, e1, e3);
  and and_4 (and_4_out, e1, e2);
  and and_5 (and_5_out, e0, not_2_out, not_3_out);
  and and_6 (and_6_out, e0, not_4_out);
  and and_7 (and_7_out, not_1_out, not_2_out);
  and and_8 (and_8_out, not_1_out, not_3_out, not_4_out);
  and and_9 (and_9_out, not_2_out, not_4_out);
  and and_10 (and_10_out, not_1_out, e2, e3);
  and and_11 (and_11_out, e0, not_3_out, e3);
  and and_12 (and_12_out, not_1_out, not_3_out);
  and and_13 (and_13_out, not_1_out, e3);
  and and_14 (and_14_out, not_3_out, e3);
  and and_15 (and_15_out, not_1_out, e1);
  and and_16 (and_16_out, e0, not_2_out);
  and and_17 (and_17_out, not_1_out, not_2_out, not_4_out);
  and and_18 (and_18_out, not_1_out, e2, not_4_out);
  and and_19 (and_19_out, not_2_out, e2, e3);
  and and_20 (and_20_out, e1, not_3_out, e3);
  and and_21 (and_21_out, e1, e2, not_4_out);
  and and_22 (and_22_out, e0, not_3_out);
  and and_23 (and_23_out, not_2_out, not_4_out);
  and and_24 (and_24_out, e2, not_4_out);
  and and_25 (and_25_out, e0, e2);
  and and_26 (and_26_out, e0, e1);
  and and_27 (and_27_out, not_3_out, not_4_out);
  and and_28 (and_28_out, not_1_out, e1, not_3_out);
  and and_29 (and_29_out, e1, not_4_out);
  and and_30 (and_30_out, e0, not_2_out);
  and and_31 (and_31_out, e0, e2);
  and and_32 (and_32_out, not_2_out, e2);
  and and_33 (and_33_out, e2, not_4_out);
  and and_34 (and_34_out, not_1_out, e1, not_3_out);
  and and_35 (and_35_out, e0, not_2_out);
  and and_36 (and_36_out, e0, e3);
  or or_1 (a, and_1_out, and_2_out, and_3_out, and_4_out, and_5_out, and_6_out);
  or or_2 (b, and_7_out, and_8_out, and_9_out, and_10_out, and_11_out);
  or or_3 (c, and_12_out, and_13_out, and_14_out, and_15_out, and_16_out);
  or or_4 (d, and_17_out, and_18_out, and_19_out, and_20_out, and_21_out, and_22_out);
  or or_5 (e, and_23_out, and_24_out, and_25_out, and_26_out);
  or or_6 (f, and_27_out, and_28_out, and_29_out, and_30_out, and_31_out);
  or or_7 (g, and_32_out, and_33_out, and_34_out, and_35_out, and_36_out);
endmodule

module compteur_synchrone_0_5 (
  input  [2:0] E,
  input  Load
);

  wire afficheur_hexa_1_a, afficheur_hexa_1_b, afficheur_hexa_1_c, afficheur_hexa_1_d, afficheur_hexa_1_e,
       afficheur_hexa_1_f, afficheur_hexa_1_g, and_1_out, and_2_out, and_3_out, and_4_out, clock_1_out,
       d_ff_1_qn, or_1_out, or_2_out, or_3_out, or_4_out, transcodeur_1_s0, transcodeur_1_s1, xor_1_out,
       xor_2_out;
  wire [2:0] controlled_buffer_1_out, d_ff_1_q;

  Clock clock_1 (.out(clock_1_out));
  D_Flip_Flop d_ff_1 (
    .D(d_ff_1_qn), .clk(clock_1_out), .Q(d_ff_1_q[0]), .Qn(d_ff_1_qn), .preset(or_1_out), .reset(and_1_out));
  and and_1 (and_1_out, d_ff_1_q[1], d_ff_1_q[2]);
  D_Flip_Flop d_ff_2 (
    .D(xor_1_out), .clk(clock_1_out), .Q(d_ff_1_q[1]), .preset(or_2_out), .reset(and_1_out));  // open: Qn
  xor xor_1 (xor_1_out, d_ff_1_q[1], d_ff_1_q[0]);
  and and_2 (and_2_out, d_ff_1_q[0], d_ff_1_q[1]);
  or or_1 (or_1_out, and_4_out, or_3_out);
  xor xor_2 (xor_2_out, d_ff_1_q[2], and_2_out);
  D_Flip_Flop d_ff_3 (
    .D(xor_2_out), .clk(clock_1_out), .Q(d_ff_1_q[2]), .preset(or_4_out), .reset(and_1_out));  // open: Qn
  transcodeur transcodeur_1 (.in_1(d_ff_1_q), .s1(transcodeur_1_s1), .s0(transcodeur_1_s0));
  or or_2 (or_2_out, and_3_out, controlled_buffer_1_out[1]);
  assign controlled_buffer_1_out = Load ? E : 3'bz;  // Controlled_Buffer controlled_buffer_1
  afficheur_hexa afficheur_hexa_1 (
    .e2(transcodeur_1_s1), .e3(transcodeur_1_s0), .a(afficheur_hexa_1_a), .b(afficheur_hexa_1_b),
    .c(afficheur_hexa_1_c), .d(afficheur_hexa_1_d), .e(afficheur_hexa_1_e), .f(afficheur_hexa_1_f),
    .g(afficheur_hexa_1_g));  // open: e0, e1
  or or_3 (or_3_out, and_3_out, controlled_buffer_1_out[0]);
  or or_4 (or_4_out, controlled_buffer_1_out[2], and_4_out);
  _7_Segment_Display u_7_segment_display_1 (
    .g(afficheur_hexa_1_g), .f(afficheur_hexa_1_f), .a(afficheur_hexa_1_a), .b(afficheur_hexa_1_b),
    .e(afficheur_hexa_1_e), .d(afficheur_hexa_1_d), .c(afficheur_hexa_1_c));  // open: dp
  and and_3 (and_3_out, controlled_buffer_1_out[0], controlled_buffer_1_out[1]);
  and and_4 (and_4_out, controlled_buffer_1_out[0], controlled_buffer_1_out[2]);
endmodule

module transcodeur (
  input  [2:0] in_1,
  output s1,
  output s0
);

  wire and_1_out, and_2_out, nand_1_out;

  and and_1 (and_1_out, in_1[0], in_1[1]);
  and and_2 (and_2_out, nand_1_out, in_1[1]);
  nand nand_1 (nand_1_out, in_1[1], and_1_out);
  assign and_2_out = and_1_out ? nand_1_out : 1'bz;  // Controlled_Buffer controlled_buffer_1
  or or_1 (s0, in_1[0], and_1_out);
  or or_2 (s1, in_1[2], and_2_out);
endmodule

module compteur_synchorne_final (
  input  [2:0] E,
  input  Load
);

  wire afficheur_hexa_1_a, afficheur_hexa_1_b, afficheur_hexa_1_c, afficheur_hexa_1_d, afficheur_hexa_1_e,
       afficheur_hexa_1_f, afficheur_hexa_1_g, and_1_out, and_2_out, and_3_out, and_4_out, and_5_out,
       and_6_out, and_7_out, clock_1_out, d_ff_1_qn, or_1_out, or_2_out, or_3_out, or_4_out,
       transcodeur_1_s0, transcodeur_1_s1, xor_1_out, xor_2_out;
  wire [2:0] d_ff_1_q;

  Clock clock_1 (.out(clock_1_out));
  or or_1 (or_1_out, E[0], and_6_out);
  or or_2 (or_2_out, and_7_out, or_1_out);
  D_Flip_Flop d_ff_1 (
    .D(d_ff_1_qn), .clk(clock_1_out), .Q(d_ff_1_q[0]), .Qn(d_ff_1_qn), .preset(and_1_out), .reset(and_2_out));
  and and_1 (and_1_out, or_2_out, Load);
  and and_2 (and_2_out, d_ff_1_q[1], d_ff_1_q[2]);
  or or_3 (or_3_out, E[1], and_6_out);
  D_Flip_Flop d_ff_2 (
    .D(xor_1_out), .clk(clock_1_out), .Q(d_ff_1_q[1]), .preset(and_3_out), .reset(and_2_out));  // open: Qn
  xor xor_1 (xor_1_out, d_ff_1_q[1], d_ff_1_q[0]);
  and and_3 (and_3_out, or_3_out, Load);
  and and_4 (and_4_out, d_ff_1_q[0], d_ff_1_q[1]);
  xor xor_2 (xor_2_out, d_ff_1_q[2], and_4_out);
  or or_4 (or_4_out, and_7_out, E[2]);
  and and_5 (and_5_out, or_4_out, Load);
  D_Flip_Flop d_ff_3 (
    .D(xor_2_out), .clk(clock_1_out), .Q(d_ff_1_q[2]), .preset(and_5_out), .reset(and_2_out));  // open: Qn
  transcodeur transcodeur_1 (.in_1(d_ff_1_q), .s1(transcodeur_1_s1), .s0(transcodeur_1_s0));
  and and_6 (and_6_out, E[0], E[1]);
  afficheur_hexa afficheur_hexa_1 (
    .e2(transcodeur_1_s1), .e3(transcodeur_1_s0), .a(afficheur_hexa_1_a), .b(afficheur_hexa_1_b),
    .c(afficheur_hexa_1_c), .d(afficheur_hexa_1_d), .e(afficheur_hexa_1_e), .f(afficheur_hexa_1_f),
    .g(afficheur_hexa_1_g));  // open: e0, e1
  and and_7 (and_7_out, E[0], E[2]);
  _7_Segment_Display u_7_segment_display_1 (
    .g(afficheur_hexa_1_g), .f(afficheur_hexa_1_f), .a(afficheur_hexa_1_a), .b(afficheur_hexa_1_b),
    .e(afficheur_hexa_1_e), .d(afficheur_hexa_1_d), .c(afficheur_hexa_1_c));  // open: dp
endmodule
